# Fritzing sketch ledbred (saved by Fritzing 0.9.6b)

parts:
  Part1 = Arduino Mega 2560 (Rev3)
  S2 = Pushbutton [package=THT]
  P1 = S1133 Si Photodiode [package="8mm Ceramic [THT]"]
  microSD1 = MicroSD Card Module
  Part2 = OLED Monochrome 128x32 SPI [part_number=661]
  Part3 = Adafruit Breadboard-Friendly NeoPixel [part_number="Adafruit #1312"]
  Part4 = Adafruit Breadboard-Friendly NeoPixel [part_number="Adafruit #1312"]
  Part5 = Adafruit Breadboard-Friendly NeoPixel [part_number="Adafruit #1312"]
  Part6 = Adafruit Breadboard-Friendly NeoPixel [part_number="Adafruit #1312"]
  ENCODER1 = Rotary Encoder with Knob
  R1 = Resistor [tolerance=±5% power=0.25 resistance=1M package=THT]

nets:
  N1: Part1.A0, P1.anode, R1.Pin_1
  N2: Part1.A1, Part2.RESET
  N3: Part1.A2, Part2.DC
  N4: Part1.A3, Part2.CS
  GND: Part1.GND, S2.leg1, P1.cathode, microSD1.GND, Part2.GND, Part3.GND, Part4.GND, Part5.GND, Part6.GND, ENCODER1.no_name_yet#2, ENCODER1.no_name_yet#5
  N5: Part1.D13_PWM, microSD1.SCK, Part2.SCLK
  N6: Part1.D12_PWM, microSD1.MISO
  N7: Part1.D11_PWM, microSD1.MOSI, Part2.MOSI
  N8: Part1.D10_PWM, microSD1.CS
  N9: Part1.D9_PWM, Part3.IN
  N10: Part1.D8_PWM, Part6.IN
  VDD: Part1.5V, microSD1.VCC, Part2.VIN, Part3.VDD, Part4.VDD, Part5.VDD, Part6.VDD, R1.Pin_0
  N11: Part1.D2_PWM, ENCODER1.no_name_yet#1
  N12: Part1.D3_PWM, ENCODER1.no_name_yet#3
  N13: Part1.D4_PWM, ENCODER1.no_name_yet#4
  N14: Part1.D5_PWM, S2.leg0
  N15: Part1.D6_PWM, Part4.IN
  N16: Part1.D7_PWM, Part5.IN

notes:
  MicroSD
  Monochrome OLED 128x32
  Pen Photodiode
  Pen Switch
  Rotary Encoder Switch
  Rotary Encoder
  Preview LED
  32x8 RGB LED Panel 1
  32x8 RGB LED Panel 2
  32x8 RGB LED Panel 3
  1MΩ
  CS
  SCK
  MOSI
  MISO
  VCC
  GND
  DATA
  CLK
  RST
  D/C
  VIN

custom parts:
  OLED Monochrome 128x32 SPI: These displays are small, only about 1" diagonal, but very readable due to the high contrast of an OLED display. This display is made of 128x32 individual white OLED pixels, each one is turned on or off by the controller chip. Because the display makes its own light, no backlight is required. This reduces the power required to run the OLED and is why the display has such high contrast; we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
  Adafruit Breadboard-Friendly NeoPixel: This is the easiest way possible to add small, bright RGB pixels to your project. We took the same technology from our Flora NeoPixels and made them breadboard friendly, with two rows of 3 x 0.1" spaced header on each side for easy soldering, chaining and breadboarding. These ultra-bright LEDs have a constant-current driver cooked right into the LED package! The pixels are chainable - so you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
  Rotary Encoder with Knob: Rotary Encoder with 1/4" Shaft and Knob
